# Fritzing sketch raspberrypiweatherstation (saved by Fritzing 0.9.3b)
circuit board: 8.46667cm x 5.64444cm

parts:
  Raspberry_Pi1 = Raspberry Pi B+
  U5 = SUP500F [package=sup500f]
  BMP1 = BMP085 Breakout  # not connected
  IC1 = MCP3008 8-channel 10-bit ADC [part_number=MCP3008]
  R11 = PHOTOCELL [package=photocell]

nets:
  GND: Raspberry_Pi1.GND, U5.GND
  N1: Raspberry_Pi1.GPIO15, U5.TX-O
  N2: Raspberry_Pi1.5V, U5.PSEL
  N3: IC1.no_name_yet, R11.P$1

custom parts:
  BMP085 Breakout: A breakout for the BMP085 barometric pressure and temperature sensor
